// Logisim project Sumador.circ as structural Verilog: 1 circuit, main circuit main
module main (
  input  mode,
  input  [15:0] b,
  input  [15:0] a,
  output [15:0] out_4,
  output [15:0] out_5,
  output out_6
);

  wire adder_1_cout;
  wire [15:0] bit_extender_1_out;

  assign bit_extender_1_out = {{15{mode}}, mode};  // Bit_Extender bit_extender_1
  assign out_4 = bit_extender_1_out ^ b;  // XOR_Gate xor_1, 16 bits wide
  Adder adder_1 (.a(out_4[7:0]), .b(a[7:0]), .out(out_5[7:0]), .cin(mode), .cout(adder_1_cout));
  Adder adder_2 (.a(out_4[15:8]), .b(a[15:8]), .out(out_5[15:8]), .cin(adder_1_cout), .cout(out_6));
endmodule
