// Logisim project ShifterLeftRight.circ as structural Verilog: 3 circuits, main circuit main
module main (
  input  [3:0] in_1,
  input  in_2,
  input  [15:0] in_3,
  output [15:0] out_4,
  output [15:0] out_5
);

  shiftLeftRightN shiftleftrightn_1 (.n(in_1), .mode(in_2), .Entrada(in_3), .Salida(out_4));
  ShifterSimplified shiftersimplified_1 (.n(in_1), .mode(in_2), .Entrada(in_3), .Salida(out_5));

  // Notes on the sheet:
  //   Shifter de 16 bits
  //   mode: Izq: 0, Der: 1
  //   n: número de corrimientos
endmodule

module shiftLeftRightN (
  input  [3:0] n,
  input  mode,
  input  [15:0] Entrada,
  output [15:0] Salida
);

  wire a1, a2, a3, b1, b2, b3, c1, c2, c3, d1, d2, d3, e1, e2, e3, f1, f2, f3, g1, g2, g3, h1, h2, h3, i1,
       i2, i3, j1, j2, j3, k1, k2, k3, l1, l2, l3, m1, m2, m3, n1, n2, n3, o1, o2, o3, p1, p2, p3;

  Multiplexer #(.select(2)) multiplexer_1 (
    .in0(Entrada[15]), .in1(Entrada[15]), .in2(Entrada[14]), .in3(1'b0), .out(a1), .sel({n[0], mode}));
  Multiplexer #(.select(2)) multiplexer_2 (.in0(a1), .in1(a1), .in2(c1), .in3(1'b0), .out(a2), .sel({n[1], mode}));
  Multiplexer #(.select(2)) multiplexer_3 (.in0(a2), .in1(a2), .in2(e2), .in3(1'b0), .out(a3), .sel({n[2], mode}));
  Multiplexer #(.select(2)) multiplexer_4 (
    .in0(a3), .in1(a3), .in2(i3), .in3(1'b0), .out(Salida[15]), .sel({n[3], mode}));
  Multiplexer #(.select(2)) multiplexer_5 (
    .in0(Entrada[14]), .in1(Entrada[14]), .in2(Entrada[13]), .in3(Entrada[15]), .out(b1), .sel({n[0], mode}));
  Multiplexer #(.select(2)) multiplexer_6 (.in0(b1), .in1(b1), .in2(d1), .in3(1'b0), .out(b2), .sel({n[1], mode}));
  Multiplexer #(.select(2)) multiplexer_7 (.in0(b2), .in1(b2), .in2(f2), .in3(1'b0), .out(b3), .sel({n[2], mode}));
  Multiplexer #(.select(2)) multiplexer_8 (
    .in0(b3), .in1(b3), .in2(j3), .in3(1'b0), .out(Salida[14]), .sel({n[3], mode}));
  Multiplexer #(.select(2)) multiplexer_9 (
    .in0(Entrada[13]), .in1(Entrada[13]), .in2(Entrada[12]), .in3(Entrada[14]), .out(c1), .sel({n[0], mode}));
  Multiplexer #(.select(2)) multiplexer_10 (.in0(c1), .in1(c1), .in2(e1), .in3(a1), .out(c2), .sel({n[1], mode}));
  Multiplexer #(.select(2)) multiplexer_11 (.in0(c2), .in1(c2), .in2(g2), .in3(1'b0), .out(c3), .sel({n[2], mode}));
  Multiplexer #(.select(2)) multiplexer_12 (
    .in0(c3), .in1(c3), .in2(k3), .in3(1'b0), .out(Salida[13]), .sel({n[3], mode}));
  Multiplexer #(.select(2)) multiplexer_13 (
    .in0(Entrada[12]), .in1(Entrada[12]), .in2(Entrada[11]), .in3(Entrada[13]), .out(d1), .sel({n[0], mode}));
  Multiplexer #(.select(2)) multiplexer_14 (.in0(d1), .in1(d1), .in2(f1), .in3(b1), .out(d2), .sel({n[1], mode}));
  Multiplexer #(.select(2)) multiplexer_15 (.in0(d2), .in1(d2), .in2(h2), .in3(1'b0), .out(d3), .sel({n[2], mode}));
  Multiplexer #(.select(2)) multiplexer_16 (
    .in0(d3), .in1(d3), .in2(l3), .in3(1'b0), .out(Salida[12]), .sel({n[3], mode}));
  Multiplexer #(.select(2)) multiplexer_17 (
    .in0(Entrada[11]), .in1(Entrada[11]), .in2(Entrada[10]), .in3(Entrada[12]), .out(e1), .sel({n[0], mode}));
  Multiplexer #(.select(2)) multiplexer_18 (.in0(e1), .in1(e1), .in2(g1), .in3(c1), .out(e2), .sel({n[1], mode}));
  Multiplexer #(.select(2)) multiplexer_19 (.in0(e2), .in1(e2), .in2(i2), .in3(a2), .out(e3), .sel({n[2], mode}));
  Multiplexer #(.select(2)) multiplexer_20 (
    .in0(e3), .in1(e3), .in2(m3), .in3(1'b0), .out(Salida[11]), .sel({n[3], mode}));
  Multiplexer #(.select(2)) multiplexer_21 (
    .in0(Entrada[10]), .in1(Entrada[10]), .in2(Entrada[9]), .in3(Entrada[11]), .out(f1), .sel({n[0], mode}));
  Multiplexer #(.select(2)) multiplexer_22 (.in0(f1), .in1(f1), .in2(h1), .in3(d1), .out(f2), .sel({n[1], mode}));
  Multiplexer #(.select(2)) multiplexer_23 (.in0(f2), .in1(f2), .in2(j2), .in3(b2), .out(f3), .sel({n[2], mode}));
  Multiplexer #(.select(2)) multiplexer_24 (
    .in0(f3), .in1(f3), .in2(n3), .in3(1'b0), .out(Salida[10]), .sel({n[3], mode}));
  Multiplexer #(.select(2)) multiplexer_25 (
    .in0(Entrada[9]), .in1(Entrada[9]), .in2(Entrada[8]), .in3(Entrada[10]), .out(g1), .sel({n[0], mode}));
  Multiplexer #(.select(2)) multiplexer_26 (.in0(g1), .in1(g1), .in2(i1), .in3(e1), .out(g2), .sel({n[1], mode}));
  Multiplexer #(.select(2)) multiplexer_27 (.in0(g2), .in1(g2), .in2(k2), .in3(c2), .out(g3), .sel({n[2], mode}));
  Multiplexer #(.select(2)) multiplexer_28 (
    .in0(g3), .in1(g3), .in2(o3), .in3(1'b0), .out(Salida[9]), .sel({n[3], mode}));
  Multiplexer #(.select(2)) multiplexer_29 (
    .in0(Entrada[8]), .in1(Entrada[8]), .in2(Entrada[7]), .in3(Entrada[9]), .out(h1), .sel({n[0], mode}));
  Multiplexer #(.select(2)) multiplexer_30 (.in0(h1), .in1(h1), .in2(j1), .in3(f1), .out(h2), .sel({n[1], mode}));
  Multiplexer #(.select(2)) multiplexer_31 (.in0(h2), .in1(h2), .in2(l2), .in3(d2), .out(h3), .sel({n[2], mode}));
  Multiplexer #(.select(2)) multiplexer_32 (
    .in0(h3), .in1(h3), .in2(p3), .in3(1'b0), .out(Salida[8]), .sel({n[3], mode}));
  Multiplexer #(.select(2)) multiplexer_33 (
    .in0(Entrada[7]), .in1(Entrada[7]), .in2(Entrada[6]), .in3(Entrada[8]), .out(i1), .sel({n[0], mode}));
  Multiplexer #(.select(2)) multiplexer_34 (.in0(i1), .in1(i1), .in2(k1), .in3(g1), .out(i2), .sel({n[1], mode}));
  Multiplexer #(.select(2)) multiplexer_35 (.in0(i2), .in1(i2), .in2(m2), .in3(e2), .out(i3), .sel({n[2], mode}));
  Multiplexer #(.select(2)) multiplexer_36 (
    .in0(i3), .in1(i3), .in2(1'b0), .in3(a3), .out(Salida[7]), .sel({n[3], mode}));
  Multiplexer #(.select(2)) multiplexer_37 (
    .in0(Entrada[6]), .in1(Entrada[6]), .in2(Entrada[5]), .in3(Entrada[7]), .out(j1), .sel({n[0], mode}));
  Multiplexer #(.select(2)) multiplexer_38 (.in0(j1), .in1(j1), .in2(l1), .in3(h1), .out(j2), .sel({n[1], mode}));
  Multiplexer #(.select(2)) multiplexer_39 (.in0(j2), .in1(j2), .in2(n2), .in3(f2), .out(j3), .sel({n[2], mode}));
  Multiplexer #(.select(2)) multiplexer_40 (
    .in0(j3), .in1(j3), .in2(1'b0), .in3(b3), .out(Salida[6]), .sel({n[3], mode}));
  Multiplexer #(.select(2)) multiplexer_41 (
    .in0(Entrada[5]), .in1(Entrada[5]), .in2(Entrada[4]), .in3(Entrada[6]), .out(k1), .sel({n[0], mode}));
  Multiplexer #(.select(2)) multiplexer_42 (.in0(k1), .in1(k1), .in2(m1), .in3(i1), .out(k2), .sel({n[1], mode}));
  Multiplexer #(.select(2)) multiplexer_43 (.in0(k2), .in1(k2), .in2(o2), .in3(g2), .out(k3), .sel({n[2], mode}));
  Multiplexer #(.select(2)) multiplexer_44 (
    .in0(k3), .in1(k3), .in2(1'b0), .in3(c3), .out(Salida[5]), .sel({n[3], mode}));
  Multiplexer #(.select(2)) multiplexer_45 (
    .in0(Entrada[4]), .in1(Entrada[4]), .in2(Entrada[3]), .in3(Entrada[5]), .out(l1), .sel({n[0], mode}));
  Multiplexer #(.select(2)) multiplexer_46 (.in0(l1), .in1(l1), .in2(n1), .in3(j1), .out(l2), .sel({n[1], mode}));
  Multiplexer #(.select(2)) multiplexer_47 (.in0(l2), .in1(l2), .in2(p2), .in3(h2), .out(l3), .sel({n[2], mode}));
  Multiplexer #(.select(2)) multiplexer_48 (
    .in0(l3), .in1(l3), .in2(1'b0), .in3(d3), .out(Salida[4]), .sel({n[3], mode}));
  Multiplexer #(.select(2)) multiplexer_49 (
    .in0(Entrada[3]), .in1(Entrada[3]), .in2(Entrada[2]), .in3(Entrada[4]), .out(m1), .sel({n[0], mode}));
  Multiplexer #(.select(2)) multiplexer_50 (.in0(m1), .in1(m1), .in2(o1), .in3(k1), .out(m2), .sel({n[1], mode}));
  Multiplexer #(.select(2)) multiplexer_51 (.in0(m2), .in1(m2), .in2(1'b0), .in3(i2), .out(m3), .sel({n[2], mode}));
  Multiplexer #(.select(2)) multiplexer_52 (
    .in0(m3), .in1(m3), .in2(1'b0), .in3(e3), .out(Salida[3]), .sel({n[3], mode}));
  Multiplexer #(.select(2)) multiplexer_53 (
    .in0(Entrada[2]), .in1(Entrada[2]), .in2(Entrada[1]), .in3(Entrada[3]), .out(n1), .sel({n[0], mode}));
  Multiplexer #(.select(2)) multiplexer_54 (.in0(n1), .in1(n1), .in2(p1), .in3(l1), .out(n2), .sel({n[1], mode}));
  Multiplexer #(.select(2)) multiplexer_55 (.in0(n2), .in1(n2), .in2(1'b0), .in3(j2), .out(n3), .sel({n[2], mode}));
  Multiplexer #(.select(2)) multiplexer_56 (
    .in0(n3), .in1(n3), .in2(1'b0), .in3(f3), .out(Salida[2]), .sel({n[3], mode}));
  Multiplexer #(.select(2)) multiplexer_57 (
    .in0(Entrada[1]), .in1(Entrada[1]), .in2(Entrada[0]), .in3(Entrada[2]), .out(o1), .sel({n[0], mode}));
  Multiplexer #(.select(2)) multiplexer_58 (.in0(o1), .in1(o1), .in2(1'b0), .in3(m1), .out(o2), .sel({n[1], mode}));
  Multiplexer #(.select(2)) multiplexer_59 (.in0(o2), .in1(o2), .in2(1'b0), .in3(k2), .out(o3), .sel({n[2], mode}));
  Multiplexer #(.select(2)) multiplexer_60 (
    .in0(o3), .in1(o3), .in2(1'b0), .in3(g3), .out(Salida[1]), .sel({n[3], mode}));
  Multiplexer #(.select(2)) multiplexer_61 (
    .in0(Entrada[0]), .in1(Entrada[0]), .in2(1'b0), .in3(Entrada[1]), .out(p1), .sel({n[0], mode}));
  Multiplexer #(.select(2)) multiplexer_62 (.in0(p1), .in1(p1), .in2(1'b0), .in3(n1), .out(p2), .sel({n[1], mode}));
  Multiplexer #(.select(2)) multiplexer_63 (.in0(p2), .in1(p2), .in2(1'b0), .in3(l2), .out(p3), .sel({n[2], mode}));
  Multiplexer #(.select(2)) multiplexer_64 (
    .in0(p3), .in1(p3), .in2(1'b0), .in3(h3), .out(Salida[0]), .sel({n[3], mode}));

  // Other names for the same wires on the sheet: p0 = Entrada[0]; o0 = Entrada[1]; n0 = Entrada[2]; m0 = Entrada[3];
  //   l0 = Entrada[4]; k0 = Entrada[5]; j0 = Entrada[6]; i0 = Entrada[7]; h0 = Entrada[8]; g0 = Entrada[9];
  //   f0 = Entrada[10]; e0 = Entrada[11]; d0 = Entrada[12]; c0 = Entrada[13]; b0 = Entrada[14]; a0 = Entrada[15];
  //   n2m[1:0] = {n[2], mode}; n3m[1:0] = {n[3], mode}; n0m[1:0] = {n[0], mode}; n1m[1:0] = {n[1], mode}

  // Notes on the sheet:
  //   n: número de corrimientos
  //   mode: Izq: 0, Der: 1
  //   n#m: bit # de n y mode concatenados
endmodule

module ShifterSimplified (
  input  [3:0] n,
  input  mode,
  input  [15:0] Entrada,
  output [15:0] Salida
);

  wire [15:0] multiplexer_1_out, multiplexer_2_out, multiplexer_3_out;

  Multiplexer #(.select(2), .width(16)) multiplexer_1 (
    .in0(Entrada), .in1(Entrada), .in2({Entrada[14:0], 1'b0}), .in3({1'b0, Entrada[15:1]}),
    .out(multiplexer_1_out), .sel({n[0], mode}));
  Multiplexer #(.select(2), .width(16)) multiplexer_2 (
    .in0(multiplexer_1_out), .in1(multiplexer_1_out), .in2({multiplexer_1_out[13:0], 2'b00}),
    .in3({2'b00, multiplexer_1_out[15:2]}), .out(multiplexer_2_out), .sel({n[1], mode}));
  Multiplexer #(.select(2), .width(16)) multiplexer_3 (
    .in0(multiplexer_2_out), .in1(multiplexer_2_out), .in2({multiplexer_2_out[11:0], 4'b0000}),
    .in3({4'b0000, multiplexer_2_out[15:4]}), .out(multiplexer_3_out), .sel({n[2], mode}));
  Multiplexer #(.select(2), .width(16)) multiplexer_4 (
    .in0(multiplexer_3_out), .in1(multiplexer_3_out), .in2({multiplexer_3_out[7:0], {8{1'b0}}}),
    .in3({{8{1'b0}}, multiplexer_3_out[15:8]}), .out(Salida), .sel({n[3], mode}));

  // Other names for the same wires on the sheet: n2m[1:0] = {n[2], mode}; n3m[1:0] = {n[3], mode};
  //   n0m[1:0] = {n[0], mode}; n1m[1:0] = {n[1], mode}

  // Notes on the sheet:
  //   n: número de corrimientos
  //   mode: Izq: 0, Der: 1
  //   n#m: bit # de n y mode concatenados
endmodule
